// Logisim project ZCS.circ as structural Verilog: 10 circuits, main circuit main
module main (
);

  prom prom_1 ();  // open: AddressBus, MEMR, DataBus
  ram_mem ram_mem_1 ();  // open: AddressBus, WE, OE, CLK, DataBus
endmodule

module alu (
  input  OE,
  input  [4:0] Operation,
  output [7:0] ALU_Out,
  output [7:0] Accumulator,
  output [7:0] Temp_Alu_in_Reg
);

  wire [7:0] adder_1_out, and_1_out, bus2buffercntrl_1_a_out, bus2buffercntrl_1_b_out,
       bus2buffercntrl_2_a_out, bus2buffercntrl_2_b_out, bus2buffercntrl_3_a_out, bus2buffercntrl_3_b_out,
       bus2buffercntrl_4_a_out, bus2buffercntrl_4_b_out, bus2buffercntrl_5_a_out, bus2buffercntrl_5_b_out,
       or_1_out, or_2_out, subtractor_1_out, xor_1_out;

  Bus2BufferCntrl bus2buffercntrl_1 (
    .A_Out(bus2buffercntrl_1_a_out), .B_Out(bus2buffercntrl_1_b_out), .A_In(Temp_Alu_in_Reg),
    .Control(Operation[0]), .B_In(Accumulator));
  Bus2BufferCntrl bus2buffercntrl_2 (
    .A_Out(bus2buffercntrl_2_a_out), .B_Out(bus2buffercntrl_2_b_out), .A_In(Temp_Alu_in_Reg),
    .Control(Operation[1]), .B_In(Accumulator));
  Bus2BufferCntrl bus2buffercntrl_3 (
    .A_Out(bus2buffercntrl_3_a_out), .B_Out(bus2buffercntrl_3_b_out), .A_In(Temp_Alu_in_Reg),
    .Control(Operation[2]), .B_In(Accumulator));
  Bus2BufferCntrl bus2buffercntrl_4 (
    .A_Out(bus2buffercntrl_4_a_out), .B_Out(bus2buffercntrl_4_b_out), .A_In(Temp_Alu_in_Reg),
    .Control(Operation[3]), .B_In(Accumulator));
  Bus2BufferCntrl bus2buffercntrl_5 (
    .A_Out(bus2buffercntrl_5_a_out), .B_Out(bus2buffercntrl_5_b_out), .A_In(Temp_Alu_in_Reg),
    .Control(Operation[4]), .B_In(Accumulator));
  Adder adder_1 (.a(bus2buffercntrl_1_a_out), .b(bus2buffercntrl_1_b_out), .out(adder_1_out));  // open: cin, cout
  Subtractor subtractor_1 (
    .a(bus2buffercntrl_2_a_out), .b(bus2buffercntrl_2_b_out), .out(subtractor_1_out));  // open: bin, bout
  assign and_1_out = bus2buffercntrl_3_a_out & bus2buffercntrl_3_b_out;  // AND_Gate and_1, 8 bits wide
  assign or_1_out = bus2buffercntrl_4_a_out | bus2buffercntrl_4_b_out;  // OR_Gate or_1, 8 bits wide
  assign xor_1_out = bus2buffercntrl_5_a_out ^ bus2buffercntrl_5_b_out;  // XOR_Gate xor_1, 8 bits wide
  BusBufferCntrl busbuffercntrl_1 (.A_Out(ALU_Out), .A_In(or_2_out), .Control(OE));
  assign or_2_out = adder_1_out | subtractor_1_out | and_1_out | or_1_out | xor_1_out;  // OR_Gate or_2, 8 bits wide
endmodule

module prom (
  input  [12:0] AddressBus,
  input  MEMR,
  output [7:0] DataBus
);

  wire [7:0] rom_1_data;

  ROM #(.addrWidth(13)) rom_1 (.addr(AddressBus), .data(rom_1_data));
  and and_1 (DataBus[0], rom_1_data[0], MEMR);
  and and_2 (DataBus[1], rom_1_data[1], MEMR);
  and and_3 (DataBus[2], rom_1_data[2], MEMR);
  and and_4 (DataBus[3], rom_1_data[3], MEMR);
  and and_5 (DataBus[4], rom_1_data[4], MEMR);
  and and_6 (DataBus[5], rom_1_data[5], MEMR);
  and and_7 (DataBus[6], rom_1_data[6], MEMR);
  and and_8 (DataBus[7], rom_1_data[7], MEMR);
endmodule

module ram_mem (
  input  [12:0] AddressBus,
  input  WE,
  input  OE,
  input  CLK,
  output [7:0] DataBus
);

  RAM #(.addrWidth(13), .databus("bidir")) ram_1 (.addr(AddressBus), .we(WE), .oe(OE), .clk(CLK), .data(DataBus));
endmodule

module cpu (
);

  wire [7:0] Accumulator_d_out, Temp_d_out;

  regs Accumulator (.D_Out(Accumulator_d_out));  // open: Data, OE, WE, R, CLK
  regs Temp (.D_Out(Temp_d_out));  // open: Data, OE, WE, R, CLK
  alu alu_1 (.Accumulator(Accumulator_d_out), .Temp_Alu_in_Reg(Temp_d_out));  // open: ALU_Out, Operation, OE
endmodule

module regs (
  input  OE,
  input  WE,
  input  R,
  input  CLK,
  output [7:0] Data,
  output [7:0] D_Out
);

  Register register_1 (.D(Data), .en(WE), .clk(CLK), .Q(D_Out), .clr(R));
  BusTrans bustrans_1 (.DIR_N(1'b1), .OE_N(OE), .A(D_Out), .B(Data));
endmodule

module BusTrans (
  input  DIR_N,
  input  OE_N,
  input  [7:0] A,
  input  [7:0] B
);

  wire and_1_out, and_2_out;

  and and_1 (and_1_out, DIR_N, ~OE_N);  // AND_Gate
  assign B[0] = and_1_out ? A[0] : 1'bz;  // Controlled_Buffer controlled_buffer_1
  assign B[1] = and_1_out ? A[1] : 1'bz;  // Controlled_Buffer controlled_buffer_2
  assign B[2] = and_1_out ? A[2] : 1'bz;  // Controlled_Buffer controlled_buffer_3
  assign B[3] = and_1_out ? A[3] : 1'bz;  // Controlled_Buffer controlled_buffer_4
  assign B[4] = and_1_out ? A[4] : 1'bz;  // Controlled_Buffer controlled_buffer_5
  assign B[5] = and_1_out ? A[5] : 1'bz;  // Controlled_Buffer controlled_buffer_6
  assign B[6] = and_1_out ? A[6] : 1'bz;  // Controlled_Buffer controlled_buffer_7
  assign B[7] = and_1_out ? A[7] : 1'bz;  // Controlled_Buffer controlled_buffer_8
  and and_2 (and_2_out, ~DIR_N, ~OE_N);  // AND_Gate
  assign A[0] = and_2_out ? B[0] : 1'bz;  // Controlled_Buffer controlled_buffer_9
  assign A[1] = and_2_out ? B[1] : 1'bz;  // Controlled_Buffer controlled_buffer_10
  assign A[2] = and_2_out ? B[2] : 1'bz;  // Controlled_Buffer controlled_buffer_11
  assign A[3] = and_2_out ? B[3] : 1'bz;  // Controlled_Buffer controlled_buffer_12
  assign A[4] = and_2_out ? B[4] : 1'bz;  // Controlled_Buffer controlled_buffer_13
  assign A[5] = and_2_out ? B[5] : 1'bz;  // Controlled_Buffer controlled_buffer_14
  assign A[6] = and_2_out ? B[6] : 1'bz;  // Controlled_Buffer controlled_buffer_15
  assign A[7] = and_2_out ? B[7] : 1'bz;  // Controlled_Buffer controlled_buffer_16
endmodule

module LogicGate (
  input  Control,
  input  [7:0] B_In,
  input  [7:0] A_In,
  output [7:0] A_Out,
  output [7:0] B_Out
);

  and and_1 (A_Out[0], A_In[0], Control);
  and and_2 (B_Out[0], B_In[0], Control);
  and and_3 (A_Out[1], A_In[1], Control);
  and and_4 (B_Out[1], B_In[1], Control);
  and and_5 (A_Out[2], A_In[2], Control);
  and and_6 (B_Out[2], B_In[2], Control);
  and and_7 (A_Out[3], A_In[3], Control);
  and and_8 (B_Out[3], B_In[3], Control);
  and and_9 (A_Out[4], A_In[4], Control);
  and and_10 (B_Out[4], B_In[4], Control);
  and and_11 (A_Out[5], A_In[5], Control);
  and and_12 (B_Out[5], B_In[5], Control);
  and and_13 (A_Out[6], A_In[6], Control);
  and and_14 (B_Out[6], B_In[6], Control);
  and and_15 (A_Out[7], A_In[7], Control);
  and and_16 (B_Out[7], B_In[7], Control);
endmodule

module Bus2BufferCntrl (
  input  Control,
  input  [7:0] B_In,
  input  [7:0] A_In,
  output [7:0] A_Out,
  output [7:0] B_Out
);

  and and_1 (A_Out[0], A_In[0], Control);
  and and_2 (B_Out[0], B_In[0], Control);
  and and_3 (A_Out[1], A_In[1], Control);
  and and_4 (B_Out[1], B_In[1], Control);
  and and_5 (A_Out[2], A_In[2], Control);
  and and_6 (B_Out[2], B_In[2], Control);
  and and_7 (A_Out[3], A_In[3], Control);
  and and_8 (B_Out[3], B_In[3], Control);
  and and_9 (A_Out[4], A_In[4], Control);
  and and_10 (B_Out[4], B_In[4], Control);
  and and_11 (A_Out[5], A_In[5], Control);
  and and_12 (B_Out[5], B_In[5], Control);
  and and_13 (A_Out[6], A_In[6], Control);
  and and_14 (B_Out[6], B_In[6], Control);
  and and_15 (A_Out[7], A_In[7], Control);
  and and_16 (B_Out[7], B_In[7], Control);
endmodule

module BusBufferCntrl (
  input  Control,
  input  [7:0] A_In,
  output [7:0] A_Out
);

  and and_1 (A_Out[0], A_In[0], Control);
  and and_2 (A_Out[1], A_In[1], Control);
  and and_3 (A_Out[2], A_In[2], Control);
  and and_4 (A_Out[3], A_In[3], Control);
  and and_5 (A_Out[4], A_In[4], Control);
  and and_6 (A_Out[5], A_In[5], Control);
  and and_7 (A_Out[6], A_In[6], Control);
  and and_8 (A_Out[7], A_In[7], Control);
endmodule
